# Fritzing sketch weather_clothing_music (saved by Fritzing 0.8.7b)
breadboards: 2

parts:
  Part1 = Arduino Mega ADK (Rev3)
  Part2 = Arduino Uno (Rev3) - ICSP
  J1 = Basic Servo
  J2 = Basic Servo
  M1 = DC Motor
  LED1 = LED - 5mm [color="Yellow (595nm)" package="5 mm [THT]"]
  U1 = LCD-16X2 [package=lcd-16x2]
  Q1 = NPN-Transistor [package="TO92 [THT]"]
  R1 = Resistor [tolerance=±5% resistance=10k package=THT]
  R2 = Resistor [tolerance=±5% resistance=10k package=THT]
  R3 = Resistor [tolerance=±5% resistance=220 package=THT]
  R5 = Trimmer Potentiometer [maximum_resistance=10kΩ package=THT]
  S3 = Pushbutton [package="[THT]"]
  R6 = Resistor [tolerance=±5% resistance=10k package=THT]
  S2 = Pushbutton [package="[THT]"]

nets (from the schematic view):
  N1: Part1.D19/RX1, U1.DB7
  N2: Part1.D18/TX1, U1.DB6
  N3: Part1.D17/RX2, U1.DB5
  N4: Part1.D16/TX2, U1.DB4
  N5: Part1.D15/RX3, U1.E
  N6: Part1.D14/TX3, U1.RS
  VCC: Part1.5V#275, Part1.5V#306, Part1.D5_PWM, Part1.D7_PWM, Part1.5V#463, J1.vcc, J2.vcc, U1.VDD, R2.Pin_1, R5.leg1, S3.Pin_1, S3.Pin_2, R6.Pin_1, S2.Pin_1, S2.Pin_2
  GND: Part1.GND, J1.gnd, J2.gnd, LED1.cathode, U1.VSS, U1.R_W, U1.K, R2.Pin_0, R5.wiper, R6.Pin_0
  N7: Part1.D12_PWM, R1.Pin_1
  N8: Part1.D9_PWM, J1.pulse
  N9: Part1.D8_PWM, J2.pulse
  N10: Part1.D6_PWM, R3.Pin_0
  N11: Part1.5V#501, U1.A
  N12: Part2.GND, M1.pin_2, Q1.E
  N13: M1.pin_1, Q1.C
  N14: LED1.anode, R3.Pin_1
  N15: U1.VO, R5.leg2
  N16: Q1.B, R1.Pin_0
  N17: S3.Pin_3, S3.Pin_4
  N18: S2.Pin_3, S2.Pin_4
